# Fritzing sketch xcsoar_remote_joystick (saved by Fritzing 0.9.6b)
circuit board: 1.85731cm x 3.3986cm

parts:
  XCSoar = Arduino Pro Micro (Clone)
  S = Momentary Switch [package=ksa_sealed_tac_switch]
  S_2 = Momentary Switch [package=ksa_sealed_tac_switch]
  SKQU = ALPS SKUQ 4 directions [package="DIP (Dual Inline) [THT]"]

nets:
  GND: XCSoar.GND, S.1, S_2.2, SKQU.GND
  N1: XCSoar.D5, SKQU.RIGHT
  N2: XCSoar.D6, SKQU.BTN
  N3: XCSoar.D7, SKQU.UP
  N4: XCSoar.D8, SKQU.LEFT
  N5: XCSoar.D9, SKQU.DOWN
  N6: XCSoar.D14, S_2.3
  N7: XCSoar.D15, S.3

custom parts:
  ALPS SKUQ 4 directions: 4 direction Joystick w. Switch
