# Fritzing sketch xcsoar_remote (saved by Fritzing 0.9.6b)
circuit board: 2.65cm x 3.55cm

parts:
  S1 = Momentary Switch [package=ksa_sealed_tac_switch]
  S3 = Momentary Switch [package=ksa_sealed_tac_switch]
  S4 = Momentary Switch [package=ksa_sealed_tac_switch]
  V1_0 = Arduino Pro Micro (Clone)
  S2 = Momentary Switch [package=ksa_sealed_tac_switch]
  S5 = Momentary Switch [package=ksa_sealed_tac_switch]

nets:
  N1: S1.1, V1_0.D7
  N2: S1.4, S3.3, S4.3, V1_0.GND, S2.1, S5.3
  N3: S3.2, V1_0.D8
  N4: S4.2, V1_0.D9
  N5: V1_0.D5, S5.1
  N6: V1_0.D6, S2.4
