# Fritzing sketch xcsoar_remote_joystick (saved by Fritzing 0.9.6b)
circuit board: 1.9749cm x 3.51069cm

parts:
  SKQU1 = ALPS SKUQ 4 directions [package="DIP (Dual Inline) [THT]"]
  V1_1 = Arduino Pro Micro (Clone)

nets:
  N1: SKQU1.DOWN, V1_1.D9
  N2: SKQU1.LEFT, V1_1.D8
  N3: SKQU1.UP, V1_1.D7
  N4: SKQU1.BTN, V1_1.D6
  N5: SKQU1.RIGHT, V1_1.D5
  GND: SKQU1.GND, V1_1.GND

custom parts:
  ALPS SKUQ 4 directions: 4 direction Joystick w. Switch
